// Logisim project parte1_cache.circ as structural Verilog: 4 circuits, main circuit main
module main (
  input  [5:0] ENDERECO,
  input  RESET,
  input  RESET_CONT,
  output DESLOCAMENTO,
  output ACERTO
);

  wire bit_validade_1_v_indice, CLK_out, detetor_primo_1_primo, not_1_out, not_2_out, or_1_out,
       xor_sintetizado_1_s, xor_sintetizado_2_s, xor_sintetizado_3_s;
  wire [2:0] TAG_dout;
  wire [3:0] counter_1_q;

  Clock CLK (.out(CLK_out));
  not not_1 (not_1_out, ACERTO);
  RAM #(.addrWidth(2), .dataWidth(3)) TAG (
    .addr(ENDERECO[2:1]), .we(not_1_out), .oe(1'b1), .clk(CLK_out), .din(ENDERECO[5:3]), .dout(TAG_dout));
  LED DESLOCAMENTO_LED (.in(ENDERECO[0]));
  bit_validade bit_validade_1 (
    .CONST(1'b1), .INDEX_A2A1(ENDERECO[2:1]), .CLK(CLK_out), .RESET(RESET), .V_INDICE(bit_validade_1_v_indice));
  detetor_primo detetor_primo_1 (.ENTRADA(ENDERECO[5:3]), .PRIMO(detetor_primo_1_primo));
  LED led_1 (.in(detetor_primo_1_primo));
  xor_sintetizado xor_sintetizado_1 (.A(ENDERECO[3]), .B(TAG_dout[0]), .S(xor_sintetizado_1_s));
  xor_sintetizado xor_sintetizado_2 (.A(ENDERECO[4]), .B(TAG_dout[1]), .S(xor_sintetizado_2_s));
  xor_sintetizado xor_sintetizado_3 (.A(ENDERECO[5]), .B(TAG_dout[2]), .S(xor_sintetizado_3_s));
  or or_1 (or_1_out, xor_sintetizado_1_s, xor_sintetizado_2_s, xor_sintetizado_3_s);
  LED led_2 (.in(ACERTO));
  not not_2 (not_2_out, or_1_out);
  and and_1 (ACERTO, not_2_out, bit_validade_1_v_indice);
  Counter #(.max('hf), .width(4)) counter_1 (
    .Q(counter_1_q), .clk(ACERTO), .clr(RESET_CONT));  // open: load, D, count, carry, up
  // BCD_to_7_Segment_decoder bcd_to_7_segment_decoder_1: pin names not known; wires that end beside it: counter_1_q
  _7_Segment_Display u_7_segment_display_1 ();  // open: g, f, a, b, e, d, c, dp

  assign DESLOCAMENTO = ENDERECO[0];

  // Notes on the sheet:
  //   A5-A4-A3-A2-A1-A0
  //   CONSTANTE 1
  //   DESLOCAMENTO A0
  //   INDEX A2-A1
  //   TAG A5-A3
  //   T0-T1-T2
  //   S0-S1-S2
  //   É_PRIMO
  //   PORTA XOR SINTETIZADAS T0,T1,T2 - S0,S1,S2
  //   BIT DE VALIDADE
  //   VALIDO
endmodule

module xor_sintetizado (
  input  A,
  input  B,
  output S
);

  wire and_1_out, and_2_out, not_1_out, not_2_out;

  not not_1 (not_1_out, B);
  not not_2 (not_2_out, A);
  and and_1 (and_1_out, A, not_1_out);
  and and_2 (and_2_out, B, not_2_out);
  or or_1 (S, and_1_out, and_2_out);
endmodule

module detetor_primo (
  input  [2:0] ENTRADA,
  output PRIMO
);

  wire and_1_out, and_2_out, not_1_out;

  not not_1 (not_1_out, ENTRADA[2]);
  and and_1 (and_1_out, ENTRADA[1], not_1_out);
  and and_2 (and_2_out, ENTRADA[0], ENTRADA[2]);
  or or_1 (PRIMO, and_1_out, and_2_out);
endmodule

module bit_validade (
  input  CONST,
  input  [1:0] INDEX_A2A1,
  input  CLK,
  input  RESET,
  output V_INDICE
);

  wire d_ff_1_q, d_ff_2_q, d_ff_3_q, d_ff_4_q, decoder_1_out0, decoder_1_out1, decoder_1_out2,
       decoder_1_out3, multiplexer_1_out, multiplexer_2_out, multiplexer_3_out, multiplexer_4_out;

  Multiplexer multiplexer_1 (.in0(d_ff_1_q), .in1(CONST), .out(multiplexer_1_out), .sel(decoder_1_out0));
  Multiplexer multiplexer_2 (.in0(d_ff_2_q), .in1(CONST), .out(multiplexer_2_out), .sel(decoder_1_out1));
  Multiplexer multiplexer_3 (.in0(d_ff_3_q), .in1(CONST), .out(multiplexer_3_out), .sel(decoder_1_out2));
  Multiplexer multiplexer_4 (.in0(d_ff_4_q), .in1(CONST), .out(multiplexer_4_out), .sel(decoder_1_out3));
  D_Flip_Flop d_ff_1 (.D(multiplexer_1_out), .clk(CLK), .Q(d_ff_1_q), .reset(RESET));  // open: Qn, preset
  D_Flip_Flop d_ff_2 (.D(multiplexer_2_out), .clk(CLK), .Q(d_ff_2_q), .reset(RESET));  // open: Qn, preset
  D_Flip_Flop d_ff_3 (.D(multiplexer_3_out), .clk(CLK), .Q(d_ff_3_q), .reset(RESET));  // open: Qn, preset
  D_Flip_Flop d_ff_4 (.D(multiplexer_4_out), .clk(CLK), .Q(d_ff_4_q), .reset(RESET));  // open: Qn, preset
  Multiplexer #(.select(2)) multiplexer_5 (
    .in0(d_ff_1_q), .in1(d_ff_2_q), .in2(d_ff_3_q), .in3(d_ff_4_q), .out(V_INDICE), .sel(INDEX_A2A1));
  Decoder #(.enable("false"), .select(2)) decoder_1 (
    .out0(decoder_1_out0), .out1(decoder_1_out1), .out2(decoder_1_out2), .out3(decoder_1_out3),
    .sel(INDEX_A2A1));
  // also tied to VCC on the sheet: decoder_1_out0

  // Notes on the sheet:
  //   BIT DE VALIDAÇÃO DE 4 LINHAS
endmodule
